// Logisim project CS3410_P1.circ as structural Verilog: 22 circuits, main circuit ALU32
module ALU32 (
  input  [31:0] B,
  input  [31:0] A,
  input  [3:0] Op,
  input  [4:0] Sa,
  output V,
  output [31:0] C
);

  wire add_subtract_1_v;
  wire [31:0] add_subtract_1_c, le_gt_1_c, logicgates_1_c, ne_eq_1_c, subshift_1_c;

  ne_eq ne_eq_1 (.A(A), .B(B), .Op(Op), .C(ne_eq_1_c));
  add_subtract add_subtract_1 (.B(B), .A(A), .Op(Op), .V(add_subtract_1_v), .C(add_subtract_1_c));
  le_gt le_gt_1 (.A(A), .Op(Op), .C(le_gt_1_c));
  logicgates logicgates_1 (.A(A), .B(B), .Op(Op), .C(logicgates_1_c));
  subshift subshift_1 (.Op(Op), .B(B), .Sa(Sa), .C(subshift_1_c));
  overflow overflow_1 (.Op(Op), .Vin(add_subtract_1_v), .Vout(V));
  opselect opselect_1 (
    .ne_eq(ne_eq_1_c), .add_subtract(add_subtract_1_c), .le_gt(le_gt_1_c), .logicgates(logicgates_1_c),
    .subshift(subshift_1_c), .Op(Op), .C(C));
endmodule

module bitshift1 (
  input  Cin,
  input  [31:0] B,
  output [31:0] C
);


  assign C = {B[30:0], Cin};
endmodule

module bitshift2 (
  input  Cin,
  input  [31:0] B,
  output [31:0] C
);

  wire [31:0] bitshift1_1_c;

  bitshift1 bitshift1_1 (.Cin(Cin), .B(B), .C(bitshift1_1_c));
  bitshift1 bitshift1_2 (.Cin(Cin), .B(bitshift1_1_c), .C(C));
endmodule

module bitshift4 (
  input  Cin,
  input  [31:0] B,
  output [31:0] C
);

  wire [31:0] bitshift2_1_c;

  bitshift2 bitshift2_1 (.Cin(Cin), .B(B), .C(bitshift2_1_c));
  bitshift2 bitshift2_2 (.Cin(Cin), .B(bitshift2_1_c), .C(C));
endmodule

module bitshift8 (
  input  Cin,
  input  [31:0] B,
  output [31:0] C
);

  wire [31:0] bitshift4_1_c;

  bitshift4 bitshift4_1 (.Cin(Cin), .B(B), .C(bitshift4_1_c));
  bitshift4 bitshift4_2 (.Cin(Cin), .B(bitshift4_1_c), .C(C));
endmodule

module bitshift16 (
  input  Cin,
  input  [31:0] B,
  output [31:0] C
);

  wire [31:0] bitshift8_1_c;

  bitshift8 bitshift8_1 (.Cin(Cin), .B(B), .C(bitshift8_1_c));
  bitshift8 bitshift8_2 (.Cin(Cin), .B(bitshift8_1_c), .C(C));
endmodule

module LeftShift32 (
  input  Cin,
  input  [31:0] B,
  input  [4:0] Sa,
  output [31:0] C
);

  wire [31:0] bitshift1_1_c, bitshift2_1_c, bitshift4_1_c, bitshift8_1_c, bitshift16_1_c, multiplexer_1_out,
       multiplexer_2_out, multiplexer_3_out, multiplexer_4_out;

  bitshift16 bitshift16_1 (.Cin(Cin), .B(B), .C(bitshift16_1_c));
  Multiplexer #(.width(32)) multiplexer_1 (.in0(B), .in1(bitshift16_1_c), .out(multiplexer_1_out), .sel(Sa[4]));
  bitshift8 bitshift8_1 (.Cin(Cin), .B(multiplexer_1_out), .C(bitshift8_1_c));
  Multiplexer #(.width(32)) multiplexer_2 (
    .in0(multiplexer_1_out), .in1(bitshift8_1_c), .out(multiplexer_2_out), .sel(Sa[3]));
  bitshift4 bitshift4_1 (.Cin(Cin), .B(multiplexer_2_out), .C(bitshift4_1_c));
  Multiplexer #(.width(32)) multiplexer_3 (
    .in0(multiplexer_2_out), .in1(bitshift4_1_c), .out(multiplexer_3_out), .sel(Sa[2]));
  bitshift2 bitshift2_1 (.Cin(Cin), .B(multiplexer_3_out), .C(bitshift2_1_c));
  Multiplexer #(.width(32)) multiplexer_4 (
    .in0(multiplexer_3_out), .in1(bitshift2_1_c), .out(multiplexer_4_out), .sel(Sa[1]));
  bitshift1 bitshift1_1 (.Cin(Cin), .B(multiplexer_4_out), .C(bitshift1_1_c));
  Multiplexer #(.width(32)) multiplexer_5 (.in0(multiplexer_4_out), .in1(bitshift1_1_c), .out(C), .sel(Sa[0]));
endmodule

module add1 (
  input  A,
  input  B,
  input  Cin,
  output S,
  output C
);

  wire and_1_out, and_2_out, xor_1_out;

  xor xor_1 (xor_1_out, A, B);
  xor xor_2 (S, xor_1_out, Cin);
  and and_1 (and_1_out, xor_1_out, Cin);
  and and_2 (and_2_out, A, B);
  or or_1 (C, and_1_out, and_2_out);
endmodule

module add4 (
  input  [3:0] A,
  input  [3:0] B,
  input  Cin,
  output V,
  output [3:0] S
);

  wire add1_1_c, add1_2_c, add1_3_c, add1_4_c;

  add1 add1_1 (.A(A[0]), .B(B[0]), .Cin(Cin), .S(S[0]), .C(add1_1_c));
  add1 add1_2 (.A(A[1]), .B(B[1]), .Cin(add1_1_c), .S(S[1]), .C(add1_2_c));
  add1 add1_3 (.A(A[2]), .B(B[2]), .Cin(add1_2_c), .S(S[2]), .C(add1_3_c));
  add1 add1_4 (.A(A[3]), .B(B[3]), .Cin(add1_3_c), .S(S[3]), .C(add1_4_c));
  xor xor_1 (V, add1_4_c, add1_3_c);
endmodule

module add4unsigned (
  input  [3:0] A,
  input  [3:0] B,
  input  Cin,
  output C,
  output [3:0] S
);

  wire add1_1_c, add1_2_c, add1_3_c;

  add1 add1_1 (.A(A[0]), .B(B[0]), .Cin(Cin), .S(S[0]), .C(add1_1_c));
  add1 add1_2 (.A(A[1]), .B(B[1]), .Cin(add1_1_c), .S(S[1]), .C(add1_2_c));
  add1 add1_3 (.A(A[2]), .B(B[2]), .Cin(add1_2_c), .S(S[2]), .C(add1_3_c));
  add1 add1_4 (.A(A[3]), .B(B[3]), .Cin(add1_3_c), .S(S[3]), .C(C));
endmodule

module add8 (
  input  [7:0] A,
  input  [7:0] B,
  input  Cin,
  output C,
  output [7:0] S
);

  wire add4unsigned_1_c;

  add4unsigned add4unsigned_1 (.A(A[3:0]), .B(B[3:0]), .Cin(Cin), .C(add4unsigned_1_c), .S(S[3:0]));
  add4unsigned add4unsigned_2 (.A(A[7:4]), .B(B[7:4]), .Cin(add4unsigned_1_c), .C(C), .S(S[7:4]));
endmodule

module add16 (
  input  [15:0] A,
  input  [15:0] B,
  input  Cin,
  output C,
  output [15:0] S
);

  wire add8_1_c;

  add8 add8_1 (.A(A[7:0]), .B(B[7:0]), .Cin(Cin), .C(add8_1_c), .S(S[7:0]));
  add8 add8_2 (.A(A[15:8]), .B(B[15:8]), .Cin(add8_1_c), .C(C), .S(S[15:8]));
endmodule

module Add32 (
  input  [31:0] B,
  input  [31:0] A,
  input  Cin,
  output V,
  output [31:0] C
);

  wire add4unsigned_1_c, add8_1_c, add16_1_c;
  wire [31:0] multiplexer_1_out, not_1_out;

  assign not_1_out = ~B;  // NOT_Gate not_1, 32 bits wide
  Multiplexer #(.width(32)) multiplexer_1 (.in0(B), .in1(not_1_out), .out(multiplexer_1_out), .sel(Cin));
  add16 add16_1 (.A(A[15:0]), .B(multiplexer_1_out[15:0]), .Cin(Cin), .C(add16_1_c), .S(C[15:0]));
  add8 add8_1 (.A(A[23:16]), .B(multiplexer_1_out[23:16]), .Cin(add16_1_c), .C(add8_1_c), .S(C[23:16]));
  add4unsigned add4unsigned_1 (
    .A(A[27:24]), .B(multiplexer_1_out[27:24]), .Cin(add8_1_c), .C(add4unsigned_1_c), .S(C[27:24]));
  add4 add4_1 (.A(A[31:28]), .B(multiplexer_1_out[31:28]), .Cin(add4unsigned_1_c), .V(V), .S(C[31:28]));
endmodule

module reverse (
  input  [31:0] X,
  output [31:0] Y
);


  assign Y = {X[0], X[1], X[2], X[3], X[4], X[5], X[6], X[7], X[8], X[9], X[10], X[11], X[12], X[13], X[14], X[15], X[16], X[17], X[18], X[19], X[20], X[21], X[22], X[23], X[24], X[25], X[26], X[27], X[28], X[29], X[30], X[31]};
endmodule

module Shift32 (
  input  Cin,
  input  [31:0] B,
  input  SL,
  input  [4:0] Sa,
  output [31:0] C
);

  wire [31:0] leftshift32_1_c, multiplexer_1_out, reverse_1_y, reverse_2_y;

  Multiplexer #(.width(32)) multiplexer_1 (.in0(B), .in1(reverse_1_y), .out(multiplexer_1_out), .sel(SL));
  reverse reverse_1 (.X(B), .Y(reverse_1_y));
  LeftShift32 leftshift32_1 (.Cin(Cin), .B(multiplexer_1_out), .Sa(Sa), .C(leftshift32_1_c));
  Multiplexer #(.width(32)) multiplexer_2 (.in0(leftshift32_1_c), .in1(reverse_2_y), .out(C), .sel(SL));
  reverse reverse_2 (.X(leftshift32_1_c), .Y(reverse_2_y));
endmodule

module subshift (
  input  [3:0] Op,
  input  [31:0] B,
  input  [4:0] Sa,
  output [31:0] C
);

  wire and_1_out, and_2_out, and_3_out;

  and and_1 (and_1_out, Op[3], Op[2]);
  and and_2 (and_2_out, and_1_out, Op[0]);
  and and_3 (and_3_out, and_2_out, B[31]);
  Shift32 shift32_1 (.Cin(and_3_out), .B(B), .SL(Op[2]), .Sa(Sa), .C(C));
endmodule

module logicgates (
  input  [31:0] A,
  input  [31:0] B,
  input  [3:0] Op,
  output [31:0] C
);

  wire [31:0] and_1_out, nor_1_out, or_1_out, xor_1_out;

  assign or_1_out = B | A;  // OR_Gate or_1, 32 bits wide
  assign and_1_out = B & A;  // AND_Gate and_1, 32 bits wide
  assign xor_1_out = B ^ A;  // XOR_Gate xor_1, 32 bits wide
  assign nor_1_out = ~(B | A);  // NOR_Gate nor_1, 32 bits wide
  Multiplexer #(.select(2), .width(32)) multiplexer_1 (
    .in0(or_1_out), .in1(and_1_out), .in2(xor_1_out), .in3(nor_1_out), .out(C), .sel(Op[1:0]));
endmodule

module ne_eq (
  input  [31:0] A,
  input  [31:0] B,
  input  [3:0] Op,
  output [31:0] C
);

  wire and_1_out, xnor_2_out;
  wire [31:0] xnor_1_out;

  assign xnor_1_out = ~(A ^ B);  // XNOR_Gate xnor_1, 32 bits wide
  and and_1 (and_1_out, xnor_1_out[0], xnor_1_out[1], xnor_1_out[2], xnor_1_out[3], xnor_1_out[4], xnor_1_out[5], xnor_1_out[6], xnor_1_out[7], xnor_1_out[8], xnor_1_out[9], xnor_1_out[10], xnor_1_out[11], xnor_1_out[12], xnor_1_out[13], xnor_1_out[14], xnor_1_out[15], xnor_1_out[17], xnor_1_out[18], xnor_1_out[19], xnor_1_out[20], xnor_1_out[21], xnor_1_out[22], xnor_1_out[23], xnor_1_out[24], xnor_1_out[25], xnor_1_out[26], xnor_1_out[27], xnor_1_out[28], xnor_1_out[29], xnor_1_out[30], xnor_1_out[31], xnor_1_out[16]);
  xnor xnor_2 (xnor_2_out, and_1_out, Op[0]);
  assign C = {{31{1'b0}}, xnor_2_out};  // Bit_Extender bit_extender_1
endmodule

module le_gt (
  input  [31:0] A,
  input  [3:0] Op,
  output [31:0] C
);

  wire nor_1_out, or_1_out, xor_1_out;

  nor nor_1 (nor_1_out, A[0], A[1], A[2], A[3], A[4], A[5], A[6], A[7], A[8], A[9], A[10], A[11], A[12], A[13], A[14], A[15], A[17], A[18], A[19], A[20], A[21], A[22], A[23], A[24], A[25], A[26], A[27], A[28], A[29], A[30], A[31], A[16]);
  or or_1 (or_1_out, A[31], nor_1_out);
  xor xor_1 (xor_1_out, or_1_out, Op[0]);
  assign C = {{31{1'b0}}, xor_1_out};  // Bit_Extender bit_extender_1
endmodule

module add_subtract (
  input  [31:0] B,
  input  [31:0] A,
  input  [3:0] Op,
  output V,
  output [31:0] C
);

  Add32 add32_1 (.B(B), .A(A), .Cin(Op[3]), .V(V), .C(C));
endmodule

module opselect (
  input  [31:0] ne_eq,
  input  [31:0] add_subtract,
  input  [31:0] le_gt,
  input  [31:0] logicgates,
  input  [31:0] subshift,
  input  [3:0] Op,
  output [31:0] C
);

  wire and_1_out, and_2_out, and_3_out, nor_1_out, nor_2_out, or_1_out, or_2_out, xor_1_out, xor_2_out;
  wire [31:0] multiplexer_1_out, multiplexer_2_out, multiplexer_3_out;

  nor nor_1 (nor_1_out, Op[3], Op[2], Op[1]);
  and and_1 (and_1_out, Op[3], Op[2], Op[1]);
  nor nor_2 (nor_2_out, Op[2], Op[1]);
  Multiplexer #(.width(32)) multiplexer_1 (.in0(add_subtract), .in1(ne_eq), .out(multiplexer_1_out), .sel(nor_1_out));
  or or_1 (or_1_out, Op[3], Op[1]);
  or or_2 (or_2_out, Op[3], Op[2]);
  and and_2 (and_2_out, Op[3], Op[2], ~Op[1]);  // AND_Gate
  and and_3 (and_3_out, Op[3], nor_2_out);
  Multiplexer #(.width(32)) multiplexer_2 (
    .in0(multiplexer_1_out), .in1(le_gt), .out(multiplexer_2_out), .sel(and_1_out));
  xor xor_1 (xor_1_out, ~or_1_out, ~or_2_out);  // XOR_Gate
  xor xor_2 (xor_2_out, and_2_out, and_3_out);
  Multiplexer #(.width(32)) multiplexer_3 (
    .in0(multiplexer_2_out), .in1(logicgates), .out(multiplexer_3_out), .sel(xor_1_out));
  Multiplexer #(.width(32)) multiplexer_4 (.in0(multiplexer_3_out), .in1(subshift), .out(C), .sel(xor_2_out));
endmodule

module overflow (
  input  [3:0] Op,
  input  Vin,
  output Vout
);

  wire and_1_out, and_2_out, and_3_out, xor_1_out;

  and and_1 (and_1_out, Op[3], ~Op[2], Op[1]);  // AND_Gate
  and and_2 (and_2_out, ~Op[3], Op[2], Op[1]);  // AND_Gate
  and and_3 (and_3_out, and_1_out, and_2_out);
  xor xor_1 (xor_1_out, and_1_out, and_2_out);
  Multiplexer multiplexer_1 (.in0(and_3_out), .in1(Vin), .out(Vout), .sel(xor_1_out));
endmodule
